# Fritzing sketch 230v to 6v converter (saved by Fritzing 0.9.6b)
breadboards: 1

parts:
  D1 = Rectifier Diode [part_number=1N4001 package="300 mil [THT]"]
  D2 = Rectifier Diode [part_number=1N4001 package="300 mil [THT]"]
  D4 = Rectifier Diode [part_number=1N4001 package="300 mil [THT]"]
  D5 = Rectifier Diode [part_number=1N4001 package="300 mil [THT]"]
  Z1 = VARISTOR [package=0402-res]
  R1 = Resistor [tolerance=±5% power=0.25 resistance=1k package=THT]
  C1 = Ceramic Capacitor [capacitance=100nF voltage=35V package="100 mil [THT, multilayer]"]
  F1 = Resettable Fuse PTC [package=ptc]
  R2 = Resistor [tolerance=±5% power=1W resistance=120 package=THT]
  C2 = Tantalum Capacitor [capacitance=1nF voltage=20V package="100 mil [THT, tantalum]"]
  R3 = Resistor [tolerance=±5% power=0.25 resistance=100 package=THT]
  D6 = Zener Diode [part_number=1N4732A breakdown_voltage=5.1V package="300 mil [THT]"]
  R4 = Resistor [tolerance=±5% power=1W resistance=1k package=THT]
  LED1 = LEDs [package=led10mm]
  Power_plug1 = Power plug
  VM1 = Multimeter (DC Voltage)
  VCC1 = Battery block 9V

nets (from the schematic view):
  N1: D1.cathode, D5.anode, Z1.1, Z1.2, R1.Pin_0, C1.0, F1.2, R2.Pin_1
  N2: D1.anode, D4.anode, C2.-, D6.anode, LED1.C, VM1.COM_Probe
  N3: D2.cathode, D5.cathode
  N4: D2.anode, D4.cathode, R1.Pin_1, C1.1
  N5: F1.1, Power_plug1.GND, VCC1.-
  N6: R2.Pin_0, Power_plug1.VCC, VCC1.+
  N7: C2.+, R3.Pin_0
  N8: R3.Pin_1, D6.cathode, R4.Pin_0, VM1.V_Probe
  N9: R4.Pin_1, LED1.A
